// Logisim project g1-1.circ as structural Verilog: 1 circuit, main circuit main
module main (
  input  in_1,
  input  in_2,
  input  in_3,
  input  in_4,
  input  in_5,
  input  in_6,
  input  in_7,
  output out_8,
  output AND,
  output OR,
  output XOR
);

  wire nand_2_out, nand_3_out, nand_4_out, nand_5_out, nand_8_out, nand_9_out;

  nand nand_1 (out_8, in_1, in_1);
  nand nand_2 (nand_2_out, in_3, in_2);
  nand nand_3 (nand_3_out, in_3, in_2);
  nand nand_4 (nand_4_out, in_4, in_5);
  nand nand_5 (nand_5_out, in_6, in_7);
  nand nand_6 (AND, nand_2_out, nand_3_out);
  nand nand_7 (OR, nand_4_out, nand_4_out);
  nand nand_8 (nand_8_out, in_6, nand_5_out);
  nand nand_9 (nand_9_out, nand_5_out, in_7);
  nand nand_10 (XOR, nand_8_out, nand_9_out);

  // Notes on the sheet:
  //   NOT
endmodule
