// Logisim project g1-3.circ as structural Verilog: 3 circuits, main circuit main
module main (
  input  [1:0] op,
  input  [31:0] in,
  input  [4:0] shamt,
  output [31:0] Result
);

  ShiftUnit shiftunit_1 (.in(in), .shamt(shamt), .op(op), .result(Result));
endmodule

module ShiftUnit (
  input  [1:0] op,
  input  [31:0] in,
  input  [4:0] shamt,
  output [31:0] result
);

  wire and_1_out;
  wire [0:0] bit_extender_1_out;
  wire [1:0] bit_extender_2_out;
  wire [3:0] bit_extender_3_out;
  wire [7:0] bit_extender_4_out;
  wire [15:0] bit_extender_5_out;
  wire [31:0] multiplexer_1_out, multiplexer_2_out, multiplexer_3_out, multiplexer_4_out;

  Bit_Extender #(.in_width(1), .out_width(1), .\type ("sign")) bit_extender_1 (
    .in(and_1_out), .out(bit_extender_1_out[0]));
  and and_1 (and_1_out, in[31], op[0]);
  Multiplexer #(.select(2), .width(32), .enable("false")) multiplexer_1 (
    .in0(in), .in1(in), .in2({in[30:0], bit_extender_1_out[0]}), .in3({bit_extender_1_out[0], in[31:1]}),
    .out(multiplexer_1_out), .sel({shamt[0], op[1]}));
  assign bit_extender_2_out = {{1{and_1_out}}, and_1_out};  // Bit_Extender bit_extender_2
  Multiplexer #(.select(2), .width(32), .enable("false")) multiplexer_2 (
    .in0(multiplexer_1_out), .in1(multiplexer_1_out), .in2({multiplexer_1_out[29:0], bit_extender_2_out}),
    .in3({bit_extender_2_out, multiplexer_1_out[31:2]}), .out(multiplexer_2_out), .sel({shamt[1], op[1]}));
  assign bit_extender_3_out = {{3{and_1_out}}, and_1_out};  // Bit_Extender bit_extender_3
  Multiplexer #(.select(2), .width(32), .enable("false")) multiplexer_3 (
    .in0(multiplexer_2_out), .in1(multiplexer_2_out), .in2({multiplexer_2_out[27:0], bit_extender_3_out}),
    .in3({bit_extender_3_out, multiplexer_2_out[31:4]}), .out(multiplexer_3_out), .sel({shamt[2], op[1]}));
  assign bit_extender_4_out = {{7{and_1_out}}, and_1_out};  // Bit_Extender bit_extender_4
  Multiplexer #(.select(2), .width(32), .enable("false")) multiplexer_4 (
    .in0(multiplexer_3_out), .in1(multiplexer_3_out), .in2({multiplexer_3_out[23:0], bit_extender_4_out}),
    .in3({bit_extender_4_out, multiplexer_3_out[31:8]}), .out(multiplexer_4_out), .sel({shamt[3], op[1]}));
  assign bit_extender_5_out = {{15{and_1_out}}, and_1_out};  // Bit_Extender bit_extender_5
  Multiplexer #(.select(2), .width(32), .enable("false")) multiplexer_5 (
    .in0(multiplexer_4_out), .in1(multiplexer_4_out), .in2({multiplexer_4_out[15:0], bit_extender_5_out}),
    .in3({bit_extender_5_out, multiplexer_4_out[31:16]}), .out(result), .sel({shamt[4], op[1]}));

  // Notes on the sheet:
  //   00=sll
  //   01=sla
  //   10=srl
  //   11=sra
endmodule

module Tester (
  input  in_1,
  input  in_2,
  output [1:0] op,
  output [31:0] in,
  output [31:0] out_5,
  output [4:0] shamt
);

  wire clock_1_out;

  Clock clock_1 (.out(clock_1_out));
  Random #(.width(32)) random_1 (.clk(clock_1_out), .next(in_1), .out(in), .clr(in_2));
  Random #(.width(5)) random_2 (.clk(clock_1_out), .next(in_1), .out(shamt), .clr(in_2));
  Random #(.width(2)) random_3 (.clk(clock_1_out), .next(in_1), .out(op), .clr(in_2));
  ShiftUnit shiftunit_1 (.in(in), .shamt(shamt), .op(op), .result(out_5));

  // Notes on the sheet:
  //   Dobbeltklik mig med nulrehånden
  //   Jeg skal stå på nul ellers kaster jeg fejl
  //   op
endmodule
