// Logisim project g2-1.circ as structural Verilog: 1 circuit, main circuit main
module main (
  input  in_1
);

  wire ALU_Control_p1, and_1_out, clock, mips_alu_1_p4, registerfile_1_p5;
  wire [4:0] multiplexer_1_out;
  wire [7:0] undriven;
  wire [31:0] adder_1_p3, adder_2_p3, bit_extender_1_out, mips_alu_1_p5, mips_ram_1_p4, mipsprogramrom_1_p2,
       mipsprogramrom_1_p3, multiplexer_2_out, multiplexer_3_out, PC_q, registerfile_1_p6;

  Register #(.width(32)) PC (.D(multiplexer_3_out), .Q(PC_q), .clk(clock), .clr(in_1));  // open: en
  // Adder adder_1: pin names not known; wires that end beside it: PC_q, 32'h4, adder_1_p3
  Clock clock_1 (.out(clock));
  // MIPSProgramROM mipsprogramrom_1: pin names not known; wires that end beside it: PC_q, mipsprogramrom_1_p2, mipsprogramrom_1_p3, clock, undriven[7]
  assign bit_extender_1_out = {{16{mipsprogramrom_1_p2[15]}}, mipsprogramrom_1_p2[15:0]};  // Bit_Extender bit_extender_1
  // PLA Control: pin names not known
  Multiplexer #(.width(5), .enable("false")) multiplexer_1 (
    .in0(mipsprogramrom_1_p2[20:16]), .in1(mipsprogramrom_1_p2[15:11]), .out(multiplexer_1_out),
    .sel(undriven[0]));
  // RegisterFile registerfile_1: pin names not known; wires that end beside it: multiplexer_1_out, mipsprogramrom_1_p2[25:21], mipsprogramrom_1_p2[20:16], in_1, registerfile_1_p5, registerfile_1_p6
  // PLA ALU_Control: pin names not known; wires that end beside it: ALU_Control_p1
  Multiplexer #(.width(32), .enable("false")) multiplexer_2 (
    .in0(registerfile_1_p6), .in1(bit_extender_1_out), .out(multiplexer_2_out), .sel(undriven[6]));
  // Adder adder_2: pin names not known; wires that end beside it: adder_1_p3, {bit_extender_1_out[29:0], 2'b00}, adder_2_p3
  // MIPS_ALU mips_alu_1: pin names not known; wires that end beside it: registerfile_1_p5, multiplexer_2_out, ALU_Control_p1, mips_alu_1_p4, mips_alu_1_p5, registerfile_1_p6, undriven[5]
  Multiplexer #(.width(32), .enable("false")) multiplexer_3 (
    .in0(adder_1_p3), .in1(adder_2_p3), .out(multiplexer_3_out), .sel(and_1_out));
  and and_1 (and_1_out, undriven[1], mips_alu_1_p4);
  Multiplexer #(.width(32), .enable("false")) multiplexer_4 (
    .in0(mips_alu_1_p5), .in1(mips_ram_1_p4), .out(mipsprogramrom_1_p3), .sel(undriven[3]));
  // MIPS_RAM mips_ram_1: pin names not known; wires that end beside it: undriven[2], clock, in_1, mips_ram_1_p4

  // Other names for the same wires on the sheet: reset = in_1

  // Notes on the sheet:
  //   address
  //   rs
  //   rt
  //   rd
  //   immediate
  //   shamt
  //   funct
  //   opcode
endmodule
