// Logisim project g3-1.circ as structural Verilog: 9 circuits, main circuit main
module main (
  input  in_1
);

  wire and_1_out, clock, mips_alu_1_p4, or_1_out, or_2_out, undriven, undriven_2;
  wire [1:0] adder_1_p4, forwarding_unit_1_a, forwarding_unit_1_b;
  wire [2:0] id_ex_1_op_2_2;
  wire [3:0] mips_alu_1_p3;
  wire [4:0] ex_mem_1_rdst_2, id_ex_1_rd_2, id_ex_1_rs_2, id_ex_1_rt_2, id_ex_1_shamt_2, mem_wb_1_rdst_2,
       multiplexer_4_out, registerfile_1_p3;
  wire [5:0] id_ex_1_funct_2;
  wire [5:4] ALUControl_p2;
  wire [11:0] Control_p3, ex_mem_1_op_2, id_ex_1_op_2, mem_wb_1_op_2;
  wire [19:0] ex_mem_1_aluresult_2;
  wire [31:0] adder_1_p3, adder_2_p3, bit_extender_1_out_3, ex_mem_1_b_2, id_ex_1_a_2, id_ex_1_b_2,
       id_ex_1_imm_2, id_ex_1_pc_4_2, if_id_1_inst_2, if_id_1_pc_4_2, mem_wb_1_aluresult_2, mem_wb_1_data_2,
       mips_alu_1_p2, mips_alu_1_p5, mips_ram_1_p7, mipsprogramrom_1_p2, multiplexer_1_out,
       multiplexer_2_out, multiplexer_5_out, multiplexer_6_out, multiplexer_7_out, multiplexer_8_out,
       multiplexer_10_out, multiplexer_11_out, PC_q, registerfile_1_p7, registerfile_1_p8;
  wire [31:20] ex_mem_1_aluresult_2_2;

  Register #(.width(32)) PC (.D(multiplexer_2_out), .Q(PC_q), .clk(clock), .clr(in_1));  // open: en
  // Adder adder_1: pin names not known; wires that end beside it: 32'h4, PC_q, adder_1_p3, adder_1_p4
  Clock clock_1 (.out(clock));
  // MIPSProgramROM mipsprogramrom_1: pin names not known; wires that end beside it: PC_q, mipsprogramrom_1_p2
  Hazard_Detection_Unit hazard_detection_unit_1 ();  // open: IF_ID_RegisterRs, ID_EX_RegisterRt, IF_ID_RegisterRt, ID_EX_MemRead, Stall
  IF_ID if_id_1 (
    .PC_4(adder_1_p3), .INST(mipsprogramrom_1_p2), .Disable(undriven), .Clock(clock),
    .PC_4_2(if_id_1_pc_4_2), .INST_2(if_id_1_inst_2), .Flush(or_1_out));
  Multiplexer #(.width(32), .enable("false")) multiplexer_1 (
    .in0(multiplexer_11_out), .in1(if_id_1_pc_4_2), .out(multiplexer_1_out), .sel(mem_wb_1_op_2[11]));
  // PLA Control: pin names not known; wires that end beside it: if_id_1_inst_2[31:26], clock, Control_p3
  or or_1 (or_1_out, or_2_out, Control_p3[10]);
  Multiplexer #(.width(32), .enable("false")) multiplexer_2 (
    .in0(multiplexer_10_out), .in1({if_id_1_pc_4_2[31:28], if_id_1_inst_2[25:0], 2'b00}),
    .out(multiplexer_2_out), .sel(Control_p3[10]));
  // RegisterFile registerfile_1: pin names not known; wires that end beside it: multiplexer_1_out, mem_wb_1_op_2[1], registerfile_1_p3, if_id_1_inst_2[25:21], if_id_1_inst_2[20:16], in_1, registerfile_1_p7, registerfile_1_p8
  Multiplexer #(.width(5), .enable("false")) multiplexer_3 (
    .in0(mem_wb_1_rdst_2), .in1({5{1'b1}}), .out(registerfile_1_p3), .sel(mem_wb_1_op_2[11]));
  Bit_extender bit_extender_1 (.in_1(if_id_1_inst_2[15:0]), .out_3(bit_extender_1_out_3), .in_2(Control_p3[2]));
  ID_EX id_ex_1 (
    .PC_4(if_id_1_pc_4_2), .Disable(undriven_2), .Clock(clock), .PC_4_2(id_ex_1_pc_4_2),
    .funct(if_id_1_inst_2[5:0]), .funct_2(id_ex_1_funct_2), .shamt(if_id_1_inst_2[10:6]),
    .shamt_2(id_ex_1_shamt_2), .imm(bit_extender_1_out_3), .imm_2(id_ex_1_imm_2), .B(registerfile_1_p8),
    .B_2(id_ex_1_b_2), .A(registerfile_1_p7), .A_2(id_ex_1_a_2), .rs(if_id_1_inst_2[25:21]),
    .rs_2(id_ex_1_rs_2), .OP(Control_p3), .OP_2({id_ex_1_op_2[11:6], id_ex_1_op_2_2, id_ex_1_op_2[2:0]}),
    .rt(if_id_1_inst_2[20:16]), .rt_2(id_ex_1_rt_2), .rd(if_id_1_inst_2[15:11]), .rd_2(id_ex_1_rd_2),
    .Flush(or_2_out));
  Multiplexer #(.width(5), .enable("false")) multiplexer_4 (
    .in0(id_ex_1_rt_2), .in1(id_ex_1_rd_2), .out(multiplexer_4_out), .sel(id_ex_1_op_2[0]));
  Multiplexer #(.select(2), .width(32), .enable("false")) multiplexer_5 (
    .in0(id_ex_1_a_2), .in1(multiplexer_11_out), .in2({ex_mem_1_aluresult_2_2, ex_mem_1_aluresult_2}),
    .out(multiplexer_5_out), .sel(forwarding_unit_1_a));  // open: in3
  Multiplexer #(.select(2), .width(32), .enable("false")) multiplexer_6 (
    .in0(id_ex_1_b_2), .in1(multiplexer_11_out), .in2({ex_mem_1_aluresult_2_2, ex_mem_1_aluresult_2}),
    .out(multiplexer_6_out), .sel(forwarding_unit_1_b));  // open: in3
  Forwarding_unit forwarding_unit_1 (
    .ID_EX_RegisterRt(id_ex_1_rt_2), .ID_EX_RegisterRs(id_ex_1_rs_2), .EX_MEM_RegisterRd(ex_mem_1_rdst_2),
    .MEM_WB_RegisterRd(mem_wb_1_rdst_2), .EX_MEM_RegWrite(ex_mem_1_op_2[8]),
    .MEM_WB_RegWrite(mem_wb_1_op_2[8]), .A(forwarding_unit_1_a), .B(forwarding_unit_1_b));
  Multiplexer #(.width(32), .enable("false")) multiplexer_7 (
    .in0(id_ex_1_pc_4_2), .in1(multiplexer_5_out), .out(multiplexer_7_out), .sel(ALUControl_p2[5]));
  Multiplexer #(.width(32), .enable("false")) multiplexer_8 (
    .in0(multiplexer_5_out), .in1({{27{1'b0}}, id_ex_1_shamt_2}), .out(multiplexer_8_out),
    .sel(ALUControl_p2[4]));
  // MIPS_ALU mips_alu_1: pin names not known; wires that end beside it: multiplexer_8_out, mips_alu_1_p2, mips_alu_1_p3, mips_alu_1_p4, mips_alu_1_p5
  Multiplexer #(.width(32), .enable("false")) multiplexer_9 (
    .in0(multiplexer_6_out), .in1(id_ex_1_imm_2), .out(mips_alu_1_p2), .sel(id_ex_1_op_2[6]));
  // PLA ALUControl: pin names not known; wires that end beside it: {id_ex_1_op_2_2, id_ex_1_funct_2}, {ALUControl_p2, mips_alu_1_p3}
  // Adder adder_2: pin names not known; wires that end beside it: multiplexer_7_out, {id_ex_1_imm_2[29:0], 2'b00}, adder_2_p3
  and and_1 (and_1_out, mips_alu_1_p4, id_ex_1_op_2[7]);
  Multiplexer #(.width(32), .enable("false")) multiplexer_10 (
    .in0(multiplexer_7_out), .in1(adder_2_p3), .out(multiplexer_10_out), .sel(and_1_out));
  or or_2 (or_2_out, ALUControl_p2[5], and_1_out);
  EX_MEM ex_mem_1 (
    .Clock(clock), .B(multiplexer_6_out), .B_2(ex_mem_1_b_2), .ALUresult(mips_alu_1_p5),
    .ALUresult_2({ex_mem_1_aluresult_2_2, ex_mem_1_aluresult_2}),
    .OP({id_ex_1_op_2[11:6], id_ex_1_op_2_2, id_ex_1_op_2[2:0]}), .OP_2(ex_mem_1_op_2),
    .RDst(multiplexer_4_out), .RDst_2(ex_mem_1_rdst_2));  // open: PC_4, Disable, PC_4_2
  // MIPS_RAM mips_ram_1: pin names not known; wires that end beside it: ex_mem_1_aluresult_2, ex_mem_1_b_2, ex_mem_1_op_2[8], ex_mem_1_op_2[9], clock, in_1, mips_ram_1_p7
  MEM_WB mem_wb_1 (
    .OP(ex_mem_1_op_2), .Clock(clock), .OP_2(mem_wb_1_op_2), .Data(mips_ram_1_p7), .Data_2(mem_wb_1_data_2),
    .ALUresult({ex_mem_1_aluresult_2_2, ex_mem_1_aluresult_2}), .ALUresult_2(mem_wb_1_aluresult_2),
    .RDst(ex_mem_1_rdst_2), .RDst_2(mem_wb_1_rdst_2));  // open: PC_4, Disable, PC_4_2
  Multiplexer #(.width(32), .enable("false")) multiplexer_11 (
    .in0(mem_wb_1_aluresult_2), .in1(mem_wb_1_data_2), .out(multiplexer_11_out), .sel(mem_wb_1_op_2[9]));

  // Other names for the same wires on the sheet: reset = in_1

  // Notes on the sheet:
  //   Enkeltcyklusarkitektur, vejledende løsning
  //   JEG ARBEJDER MED BILLEDE 358
  //   MUXNE SKAL TILSLUTTES
  //   JEG FORTSÆTTER IMORGEN
  //   Den Søren!
  //   address
  //   immediate
  //   shamt
  //   funct
  //   opcode
  //   rs
  //   rt
  //   rd
  //   JUMP virker (husk at flushe IF)
  //   JAL virker (husk at flushe IF)
  //   RegWrite
  //   SignExt
  //   JumpLink
  //   Jump
  //   RegDst
  //   JUMPR HER
  //   JumpR
  //   Shamt
  //   ALUOp
  //   ALUSrc
  //   MemWrite
  //   ALUOp
  //   Branch
  //   BEQ HER
  //   MemWrite
  //   MemRead
  //   MemRead
endmodule

module Bit_extender (
  input  [15:0] in_1,
  input  in_2,
  output [31:0] out_3
);

  wire [31:0] bit_extender_1_out, bit_extender_2_out;

  assign bit_extender_1_out = {{16{1'b0}}, in_1};  // Bit_Extender bit_extender_1
  assign bit_extender_2_out = {{16{in_1[15]}}, in_1};  // Bit_Extender bit_extender_2
  Multiplexer #(.width(32), .enable("false")) multiplexer_1 (
    .in0(bit_extender_1_out), .in1(bit_extender_2_out), .out(out_3), .sel(in_2));
endmodule

module Branch_prediction_table (
  input  [24:0] TagWrite,
  input  [1:0] PWrite,
  input  [31:0] TargetWrite,
  input  Clock,
  input  write,
  input  [4:0] IndexWrite,
  input  [4:0] Index,
  input  Clear,
  output [24:0] Tag,
  output [1:0] P,
  output [31:0] Target
);

  wire [31:27] registerfile_1_p1, registerfile_1_p7;

  // RegisterFile registerfile_1: pin names not known; wires that end beside it: {registerfile_1_p1, PWrite, TagWrite}, Clock, write, IndexWrite, Index, Clear, {registerfile_1_p7, P, Tag}
  // RegisterFile registerfile_2: pin names not known; wires that end beside it: TargetWrite, Clock, write, IndexWrite, Index, Clear, Target
endmodule

module Hazard_Detection_Unit (
  input  [31:0] IF_ID_RegisterRs,
  input  [31:0] ID_EX_RegisterRt,
  input  [31:0] IF_ID_RegisterRt,
  input  ID_EX_MemRead,
  output Stall
);

  wire comparator_1_eq, comparator_2_eq, or_1_out;

  Comparator #(.width(32)) comparator_1 (
    .a(IF_ID_RegisterRs), .b(ID_EX_RegisterRt), .eq(comparator_1_eq));  // open: gt, lt
  Comparator #(.width(32)) comparator_2 (
    .a(ID_EX_RegisterRt), .b(IF_ID_RegisterRt), .eq(comparator_2_eq));  // open: gt, lt
  or or_1 (or_1_out, comparator_1_eq, comparator_2_eq);
  and and_1 (Stall, or_1_out, ID_EX_MemRead);
endmodule

module Forwarding_unit (
  input  [4:0] ID_EX_RegisterRt,
  input  [4:0] ID_EX_RegisterRs,
  input  [4:0] EX_MEM_RegisterRd,
  input  [4:0] MEM_WB_RegisterRd,
  input  EX_MEM_RegWrite,
  input  MEM_WB_RegWrite,
  output [1:0] A,
  output [1:0] B
);

  wire and_1_out, and_2_out, comparator_1_eq, comparator_2_eq, comparator_3_eq, comparator_4_eq,
       comparator_5_eq, comparator_6_eq;

  and and_1 (and_1_out, EX_MEM_RegWrite, 1'b1);
  and and_2 (and_2_out, MEM_WB_RegWrite, 1'b1);
  Comparator #(.width(5)) comparator_1 (
    .a(ID_EX_RegisterRt), .b(EX_MEM_RegisterRd), .eq(comparator_1_eq));  // open: gt, lt
  Comparator #(.width(5)) comparator_2 (
    .a(ID_EX_RegisterRs), .b(EX_MEM_RegisterRd), .eq(comparator_2_eq));  // open: gt, lt
  Comparator #(.width(5)) comparator_3 (.a(EX_MEM_RegisterRd), .b({5{1'b0}}), .eq(comparator_3_eq));  // open: gt, lt
  Comparator #(.width(5)) comparator_4 (.a(MEM_WB_RegisterRd), .b({5{1'b0}}), .eq(comparator_4_eq));  // open: gt, lt
  Comparator #(.width(5)) comparator_5 (
    .a(MEM_WB_RegisterRd), .b(ID_EX_RegisterRt), .eq(comparator_5_eq));  // open: gt, lt
  and and_3 (A[1], comparator_1_eq, ~comparator_3_eq, and_1_out);  // AND_Gate
  Comparator #(.width(5)) comparator_6 (
    .a(ID_EX_RegisterRs), .b(MEM_WB_RegisterRd), .eq(comparator_6_eq));  // open: gt, lt
  and and_4 (B[1], comparator_2_eq, ~comparator_3_eq, and_1_out);  // AND_Gate
  and and_5 (A[0], comparator_5_eq, ~A[1], ~comparator_4_eq, and_2_out);  // AND_Gate
  and and_6 (B[0], comparator_6_eq, ~B[1], ~comparator_4_eq, and_2_out);  // AND_Gate
endmodule

module IF_ID (
  input  [31:0] PC_4,
  input  [31:0] INST,
  input  Disable,
  input  Clock,
  input  Flush,
  output [31:0] PC_4_2,
  output [31:0] INST_2
);

  wire not_1_out;
  wire [31:0] multiplexer_1_out;

  Multiplexer #(.width(32), .enable("false")) multiplexer_1 (
    .in0(INST), .in1({32{1'b0}}), .out(multiplexer_1_out), .sel(Flush));
  not not_1 (not_1_out, Disable);
  Register #(.width(32), .trigger("falling")) register_1 (
    .D(PC_4), .en(not_1_out), .Q(PC_4_2), .clk(Clock));  // open: clr
  Register #(.width(32), .trigger("falling")) register_2 (
    .D(multiplexer_1_out), .en(not_1_out), .Q(INST_2), .clk(Clock));  // open: clr
endmodule

module ID_EX (
  input  [31:0] PC_4,
  input  [31:0] A,
  input  [31:0] B,
  input  [31:0] imm,
  input  [4:0] shamt,
  input  [5:0] funct,
  input  [11:0] OP,
  input  Flush,
  input  [4:0] rs,
  input  [4:0] rt,
  input  [4:0] rd,
  input  Disable,
  input  Clock,
  output [31:0] PC_4_2,
  output [31:0] A_2,
  output [31:0] B_2,
  output [31:0] imm_2,
  output [4:0] shamt_2,
  output [5:0] funct_2,
  output [11:0] OP_2,
  output [4:0] rs_2,
  output [4:0] rt_2,
  output [4:0] rd_2
);

  wire not_1_out;
  wire [11:0] multiplexer_1_out;

  Multiplexer #(.width(12), .enable("false")) multiplexer_1 (
    .in0(OP), .in1({12{1'b0}}), .out(multiplexer_1_out), .sel(Flush));
  not not_1 (not_1_out, Disable);
  Register #(.width(32), .trigger("falling")) register_1 (
    .D(PC_4), .en(not_1_out), .Q(PC_4_2), .clk(Clock));  // open: clr
  Register #(.width(32), .trigger("falling")) register_2 (.D(A), .en(not_1_out), .Q(A_2), .clk(Clock));  // open: clr
  Register #(.width(32), .trigger("falling")) register_3 (.D(B), .en(not_1_out), .Q(B_2), .clk(Clock));  // open: clr
  Register #(.width(32), .trigger("falling")) register_4 (
    .D(imm), .en(not_1_out), .Q(imm_2), .clk(Clock));  // open: clr
  Register #(.width(5), .trigger("falling")) register_5 (
    .D(shamt), .en(not_1_out), .Q(shamt_2), .clk(Clock));  // open: clr
  Register #(.width(6), .trigger("falling")) register_6 (
    .D(funct), .en(not_1_out), .Q(funct_2), .clk(Clock));  // open: clr
  Register #(.width(12), .trigger("falling")) register_7 (
    .D(multiplexer_1_out), .en(not_1_out), .Q(OP_2), .clk(Clock));  // open: clr
  Register #(.width(5), .trigger("falling")) register_8 (.D(rs), .en(not_1_out), .Q(rs_2), .clk(Clock));  // open: clr
  Register #(.width(5), .trigger("falling")) register_9 (.D(rt), .en(not_1_out), .Q(rt_2), .clk(Clock));  // open: clr
  Register #(.width(5), .trigger("falling")) register_10 (.D(rd), .en(not_1_out), .Q(rd_2), .clk(Clock));  // open: clr
endmodule

module EX_MEM (
  input  [31:0] PC_4,
  input  [31:0] ALUresult,
  input  [31:0] B,
  input  [11:0] OP,
  input  [4:0] RDst,
  input  Disable,
  input  Clock,
  output [31:0] PC_4_2,
  output [31:0] ALUresult_2,
  output [31:0] B_2,
  output [11:0] OP_2,
  output [4:0] RDst_2
);

  wire not_1_out;

  not not_1 (not_1_out, Disable);
  Register #(.width(32), .trigger("falling")) register_1 (
    .D(PC_4), .en(not_1_out), .Q(PC_4_2), .clk(Clock));  // open: clr
  Register #(.width(32), .trigger("falling")) register_2 (
    .D(ALUresult), .en(not_1_out), .Q(ALUresult_2), .clk(Clock));  // open: clr
  Register #(.width(32), .trigger("falling")) register_3 (.D(B), .en(not_1_out), .Q(B_2), .clk(Clock));  // open: clr
  Register #(.width(12), .trigger("falling")) register_4 (.D(OP), .en(not_1_out), .Q(OP_2), .clk(Clock));  // open: clr
  Register #(.width(5), .trigger("falling")) register_5 (
    .D(RDst), .en(not_1_out), .Q(RDst_2), .clk(Clock));  // open: clr
endmodule

module MEM_WB (
  input  [31:0] PC_4,
  input  [31:0] ALUresult,
  input  [31:0] Data,
  input  [11:0] OP,
  input  [4:0] RDst,
  input  Disable,
  input  Clock,
  output [31:0] PC_4_2,
  output [31:0] ALUresult_2,
  output [31:0] Data_2,
  output [11:0] OP_2,
  output [4:0] RDst_2
);

  wire not_1_out;

  not not_1 (not_1_out, Disable);
  Register #(.width(32), .trigger("falling")) register_1 (
    .D(PC_4), .en(not_1_out), .Q(PC_4_2), .clk(Clock));  // open: clr
  Register #(.width(32), .trigger("falling")) register_2 (
    .D(ALUresult), .en(not_1_out), .Q(ALUresult_2), .clk(Clock));  // open: clr
  Register #(.width(32), .trigger("falling")) register_3 (
    .D(Data), .en(not_1_out), .Q(Data_2), .clk(Clock));  // open: clr
  Register #(.width(12), .trigger("falling")) register_4 (.D(OP), .en(not_1_out), .Q(OP_2), .clk(Clock));  // open: clr
  Register #(.width(5), .trigger("falling")) register_5 (
    .D(RDst), .en(not_1_out), .Q(RDst_2), .clk(Clock));  // open: clr
endmodule
