// Logisim project g3-2.circ as structural Verilog: 13 circuits, main circuit main
module main (
  input  in_1
);

  wire branch_guessing_unit_1_out, clock, hazard_detection_unit_1_stall, id_ex_1_branch_guess_2,
       if_id_1_branch_guess_2, jump_n_branch_1_p_increment, mips_alu_1_p4, not_1_out, or_1_out, or_2_out;
  wire [1:0] branch_prediction_table_1_p, forwarding_unit_1_a, forwarding_unit_1_b, id_ex_1_p_2,
       id_ex_1_pc_4_2, if_id_1_p_2, jump_n_branch_1_flushing, p_unit_1_out_3;
  wire [2:0] id_ex_1_op_2_2;
  wire [4:0] adder_1_p3_2, ex_mem_1_rdst_2, id_ex_1_pc_4_2_2, id_ex_1_rd_2, id_ex_1_rs_2, id_ex_1_rt_2,
       id_ex_1_shamt_2, multiplexer_3_out, multiplexer_4_out, registerfile_1_p3;
  wire [5:0] id_ex_1_funct_2, mips_alu_1_p3;
  wire [11:0] Control_p3, ex_mem_1_op_2, id_ex_1_op_2, mem_wb_1_op_2;
  wire [24:0] branch_prediction_table_1_tag, id_ex_1_pc_4_2_3;
  wire [27:0] if_id_1_pc_4_2;
  wire [31:0] adder_1_p3, bit_extender_1_out_3, branch_prediction_table_1_target, ex_mem_1_aluresult_2,
       ex_mem_1_b_2, ex_mem_1_pc_4_2, id_ex_1_a_2, id_ex_1_b_2, id_ex_1_imm_2, id_ex_1_target_2,
       if_id_1_target_2, jump_n_branch_1_pcnew, jump_n_branch_1_target_2, mem_wb_1_aluresult_2,
       mem_wb_1_data_2, mem_wb_1_pc_4_2, mips_alu_1_p5, mips_ram_1_p7, mipsprogramrom_1_p2,
       multiplexer_1_out, multiplexer_2_out, multiplexer_5_out, multiplexer_6_out, multiplexer_7_out,
       multiplexer_8_out, multiplexer_9_out, PC_q, registerfile_1_p1, registerfile_1_p7, registerfile_1_p8;
  wire [31:2] if_id_1_inst_2;
  wire [31:26] if_id_1_inst_2_2;

  not not_1 (not_1_out, hazard_detection_unit_1_stall);
  Register #(.width(32)) PC (.D(multiplexer_1_out), .en(not_1_out), .Q(PC_q), .clk(clock), .clr(in_1));
  Clock clock_1 (.out(clock));
  Multiplexer #(.select(2), .width(32), .enable("false")) multiplexer_1 (
    .in0(multiplexer_2_out), .in1({if_id_1_inst_2, 2'b00}), .in2(jump_n_branch_1_pcnew),
    .in3(jump_n_branch_1_pcnew), .out(multiplexer_1_out), .sel(jump_n_branch_1_flushing));
  // Adder adder_1: pin names not known; wires that end beside it: 32'h4, PC_q, {adder_1_p3[31:7], adder_1_p3_2, adder_1_p3[1:0]}
  Branch_Guessing_Unit branch_guessing_unit_1 (
    .Tag(branch_prediction_table_1_tag), .PC({adder_1_p3[31:7], adder_1_p3_2, adder_1_p3[1:0]}),
    .P(branch_prediction_table_1_p), .Out(branch_guessing_unit_1_out));
  Branch_prediction_table branch_prediction_table_1 (
    .PWrite(p_unit_1_out_3), .TagWrite(id_ex_1_pc_4_2_3), .TargetWrite(jump_n_branch_1_target_2),
    .P(branch_prediction_table_1_p), .Tag(branch_prediction_table_1_tag),
    .Target(branch_prediction_table_1_target), .Clock(clock), .write(id_ex_1_op_2[7]),
    .IndexWrite(id_ex_1_pc_4_2_2), .Index(adder_1_p3_2));  // open: Clear
  Multiplexer #(.width(32), .enable("false")) multiplexer_2 (
    .in0({adder_1_p3[31:7], adder_1_p3_2, adder_1_p3[1:0]}), .in1(branch_prediction_table_1_target),
    .out(multiplexer_2_out), .sel(branch_guessing_unit_1_out));
  // MIPSProgramROM mipsprogramrom_1: pin names not known; wires that end beside it: PC_q, mipsprogramrom_1_p2
  IF_ID if_id_1 (
    .PC_4({adder_1_p3[31:7], adder_1_p3_2, adder_1_p3[1:0]}), .INST(mipsprogramrom_1_p2),
    .Disable(hazard_detection_unit_1_stall), .Clock(clock), .PC_4_2({if_id_1_inst_2[31:28], if_id_1_pc_4_2}),
    .INST_2({if_id_1_inst_2_2, if_id_1_inst_2[27:2]}), .Flush(or_1_out), .P(branch_prediction_table_1_p),
    .P_2(if_id_1_p_2), .Target(branch_prediction_table_1_target), .Target_2(if_id_1_target_2),
    .Branch_Guess(branch_guessing_unit_1_out), .Branch_Guess_2(if_id_1_branch_guess_2));  // open: TAG, TAG_2
  // PLA Control: pin names not known; wires that end beside it: if_id_1_inst_2_2, clock, {Control_p3[11], jump_n_branch_1_flushing[0], Control_p3[9:0]}
  or or_1 (or_1_out, jump_n_branch_1_flushing[1], jump_n_branch_1_flushing[0]);
  Hazard_Detection_Unit hazard_detection_unit_1 (
    .IF_ID_RegisterRs(if_id_1_inst_2[27:23]), .ID_EX_RegisterRt(id_ex_1_rt_2),
    .IF_ID_RegisterRt(if_id_1_inst_2[22:18]), .ID_EX_MemRead(id_ex_1_op_2[9]),
    .Stall(hazard_detection_unit_1_stall));
  // RegisterFile registerfile_1: pin names not known; wires that end beside it: registerfile_1_p1, mem_wb_1_op_2[1], registerfile_1_p3, if_id_1_inst_2[27:23], if_id_1_inst_2[22:18], in_1, registerfile_1_p7, registerfile_1_p8
  Bit_extender bit_extender_1 (.in_1(if_id_1_inst_2[17:2]), .out_3(bit_extender_1_out_3), .in_2(Control_p3[2]));
  Multiplexer #(.width(5), .enable("false")) multiplexer_3 (
    .in0(if_id_1_inst_2[17:13]), .in1({5{1'b1}}), .out(multiplexer_3_out), .sel(Control_p3[11]));
  or or_2 (or_2_out, hazard_detection_unit_1_stall, jump_n_branch_1_flushing[1]);
  ID_EX id_ex_1 (
    .PC_4({if_id_1_inst_2[31:28], if_id_1_pc_4_2}), .Clock(clock),
    .PC_4_2({id_ex_1_pc_4_2_3, id_ex_1_pc_4_2_2, id_ex_1_pc_4_2}), .funct(if_id_1_inst_2[7:2]),
    .funct_2(id_ex_1_funct_2), .shamt(if_id_1_inst_2[12:8]), .shamt_2(id_ex_1_shamt_2),
    .imm(bit_extender_1_out_3), .imm_2(id_ex_1_imm_2), .B(registerfile_1_p8), .B_2(id_ex_1_b_2),
    .A(registerfile_1_p7), .A_2(id_ex_1_a_2), .rs(if_id_1_inst_2[27:23]), .rs_2(id_ex_1_rs_2),
    .OP({Control_p3[11], jump_n_branch_1_flushing[0], Control_p3[9:0]}),
    .OP_2({id_ex_1_op_2[11:6], id_ex_1_op_2_2, id_ex_1_op_2[2:0]}), .rt(if_id_1_inst_2[22:18]),
    .rt_2(id_ex_1_rt_2), .rd(multiplexer_3_out), .rd_2(id_ex_1_rd_2), .Flush(or_2_out), .P(if_id_1_p_2),
    .P_2(id_ex_1_p_2), .Target(if_id_1_target_2), .Target_2(id_ex_1_target_2),
    .Branch_Guess(if_id_1_branch_guess_2), .Branch_Guess_2(id_ex_1_branch_guess_2));  // open: Disable, TAG, TAG_2
  P_unit p_unit_1 (.out_3(p_unit_1_out_3), .P(id_ex_1_p_2), .Increment(jump_n_branch_1_p_increment));
  Multiplexer #(.width(5), .enable("false")) multiplexer_4 (
    .in0(id_ex_1_rt_2), .in1(id_ex_1_rd_2), .out(multiplexer_4_out), .sel(id_ex_1_op_2[0]));
  Multiplexer #(.select(2), .width(32), .enable("false")) multiplexer_5 (
    .in0(id_ex_1_a_2), .in1(registerfile_1_p1), .in2(ex_mem_1_aluresult_2), .out(multiplexer_5_out),
    .sel(forwarding_unit_1_a));  // open: in3
  Multiplexer #(.select(2), .width(32), .enable("false")) multiplexer_6 (
    .in0(id_ex_1_b_2), .in1(registerfile_1_p1), .in2(ex_mem_1_aluresult_2), .out(multiplexer_6_out),
    .sel(forwarding_unit_1_b));  // open: in3
  Forwarding_unit forwarding_unit_1 (
    .ID_EX_RegisterRt(id_ex_1_rt_2), .ID_EX_RegisterRs(id_ex_1_rs_2), .EX_MEM_RegisterRd(ex_mem_1_rdst_2),
    .MEM_WB_RegisterRd(registerfile_1_p3), .EX_MEM_RegWrite(ex_mem_1_op_2[1]),
    .MEM_WB_RegWrite(mem_wb_1_op_2[1]), .B(forwarding_unit_1_b), .A(forwarding_unit_1_a));
  Multiplexer #(.width(32), .enable("false")) multiplexer_7 (
    .in0(multiplexer_5_out), .in1({{27{1'b0}}, id_ex_1_shamt_2}), .out(multiplexer_7_out),
    .sel(mips_alu_1_p3[4]));
  Multiplexer #(.width(32), .enable("false")) multiplexer_8 (
    .in0(multiplexer_6_out), .in1(id_ex_1_imm_2), .out(multiplexer_8_out), .sel(id_ex_1_op_2[6]));
  Jump_n_Branch jump_n_branch_1 (
    .PC_4({id_ex_1_pc_4_2_3, id_ex_1_pc_4_2_2, id_ex_1_pc_4_2}), .Amux(multiplexer_5_out),
    .ImmideateExt(id_ex_1_imm_2), .ALUcontrol(mips_alu_1_p3), .ALUzero(mips_alu_1_p4),
    .Branch(id_ex_1_op_2[7]), .PCnew(jump_n_branch_1_pcnew), .Flushing(jump_n_branch_1_flushing[1]),
    .Target(id_ex_1_target_2), .Branch_Guess(id_ex_1_branch_guess_2),
    .P_Increment(jump_n_branch_1_p_increment), .Target_2(jump_n_branch_1_target_2));
  // MIPS_ALU mips_alu_1: pin names not known; wires that end beside it: multiplexer_7_out, multiplexer_8_out, mips_alu_1_p3[3:0], mips_alu_1_p4, mips_alu_1_p5
  // PLA ALUControl: pin names not known; wires that end beside it: {id_ex_1_op_2_2, id_ex_1_funct_2}, mips_alu_1_p3
  EX_MEM ex_mem_1 (
    .PC_4({id_ex_1_pc_4_2_3, id_ex_1_pc_4_2_2, id_ex_1_pc_4_2}), .Clock(clock), .PC_4_2(ex_mem_1_pc_4_2),
    .B(multiplexer_6_out), .B_2(ex_mem_1_b_2), .ALUresult(mips_alu_1_p5), .ALUresult_2(ex_mem_1_aluresult_2),
    .OP({id_ex_1_op_2[11:6], id_ex_1_op_2_2, id_ex_1_op_2[2:0]}), .OP_2(ex_mem_1_op_2),
    .RDst(multiplexer_4_out), .RDst_2(ex_mem_1_rdst_2));  // open: Disable
  // MIPS_RAM mips_ram_1: pin names not known; wires that end beside it: ex_mem_1_aluresult_2[19:0], ex_mem_1_b_2, ex_mem_1_op_2[8], ex_mem_1_op_2[9], clock, in_1, mips_ram_1_p7
  MEM_WB mem_wb_1 (
    .PC_4(ex_mem_1_pc_4_2), .OP(ex_mem_1_op_2), .Clock(clock), .PC_4_2(mem_wb_1_pc_4_2),
    .OP_2(mem_wb_1_op_2), .Data(mips_ram_1_p7), .Data_2(mem_wb_1_data_2), .ALUresult(ex_mem_1_aluresult_2),
    .ALUresult_2(mem_wb_1_aluresult_2), .RDst(ex_mem_1_rdst_2), .RDst_2(registerfile_1_p3));  // open: Disable
  Multiplexer #(.width(32), .enable("false")) multiplexer_9 (
    .in0(mem_wb_1_aluresult_2), .in1(mem_wb_1_data_2), .out(multiplexer_9_out), .sel(mem_wb_1_op_2[9]));
  Multiplexer #(.width(32), .enable("false")) multiplexer_10 (
    .in0(multiplexer_9_out), .in1(mem_wb_1_pc_4_2), .out(registerfile_1_p1), .sel(mem_wb_1_op_2[11]));

  // Other names for the same wires on the sheet: reset = in_1

  // Notes on the sheet:
  //   address
  //   immediate
  //   shamt
  //   funct
  //   opcode
  //   rs
  //   rt
  //   rd
  //   RegWrite
  //   SignExt
  //   Jump
  //   JumpLink
  //   RegDst
  //   MemRead
  //   ALUOp
  //   RegWrite
  //   Not this
  //   Shamt
  //   ALUSrc
  //   ALUOp
  //   Branch
  //   RegWrite
  //   MemWrite
  //   MemRead
  //   MemRead
  //   JumpLink
endmodule

module Bit_extender (
  input  [15:0] in_1,
  input  in_2,
  output [31:0] out_3
);

  wire [31:0] bit_extender_1_out, bit_extender_2_out;

  assign bit_extender_1_out = {{16{1'b0}}, in_1};  // Bit_Extender bit_extender_1
  assign bit_extender_2_out = {{16{in_1[15]}}, in_1};  // Bit_Extender bit_extender_2
  Multiplexer #(.width(32), .enable("false")) multiplexer_1 (
    .in0(bit_extender_1_out), .in1(bit_extender_2_out), .out(out_3), .sel(in_2));
endmodule

module Branch_prediction_table (
  input  [24:0] TagWrite,
  input  [1:0] PWrite,
  input  [31:0] TargetWrite,
  input  Clock,
  input  write,
  input  [4:0] IndexWrite,
  input  [4:0] Index,
  input  Clear,
  output [24:0] Tag,
  output [1:0] P,
  output [31:0] Target
);

  wire [31:27] registerfile_1_p1, registerfile_1_p7;

  // RegisterFile registerfile_1: pin names not known; wires that end beside it: {registerfile_1_p1, PWrite, TagWrite}, Clock, write, IndexWrite, Index, Clear, {registerfile_1_p7, P, Tag}
  // RegisterFile registerfile_2: pin names not known; wires that end beside it: TargetWrite, Clock, write, IndexWrite, Index, Clear, Target
endmodule

module Hazard_Detection_Unit (
  input  [4:0] IF_ID_RegisterRs,
  input  [4:0] ID_EX_RegisterRt,
  input  [4:0] IF_ID_RegisterRt,
  input  ID_EX_MemRead,
  output Stall
);

  wire comparator_1_eq, comparator_2_eq, or_1_out;

  Comparator #(.width(5)) comparator_1 (
    .a(IF_ID_RegisterRs), .b(ID_EX_RegisterRt), .eq(comparator_1_eq));  // open: gt, lt
  Comparator #(.width(5)) comparator_2 (
    .a(ID_EX_RegisterRt), .b(IF_ID_RegisterRt), .eq(comparator_2_eq));  // open: gt, lt
  or or_1 (or_1_out, comparator_1_eq, comparator_2_eq);
  and and_1 (Stall, or_1_out, ID_EX_MemRead);
endmodule

module Forwarding_unit (
  input  [4:0] ID_EX_RegisterRt,
  input  [4:0] ID_EX_RegisterRs,
  input  [4:0] EX_MEM_RegisterRd,
  input  [4:0] MEM_WB_RegisterRd,
  input  EX_MEM_RegWrite,
  input  MEM_WB_RegWrite,
  output [1:0] B,
  output [1:0] A
);

  wire and_1_out, and_2_out, comparator_1_eq, comparator_2_eq, comparator_3_eq, comparator_4_eq,
       comparator_5_eq, comparator_6_eq;

  and and_1 (and_1_out, EX_MEM_RegWrite, 1'b1);
  and and_2 (and_2_out, MEM_WB_RegWrite, 1'b1);
  Comparator #(.width(5)) comparator_1 (
    .a(ID_EX_RegisterRt), .b(EX_MEM_RegisterRd), .eq(comparator_1_eq));  // open: gt, lt
  Comparator #(.width(5)) comparator_2 (
    .a(ID_EX_RegisterRs), .b(EX_MEM_RegisterRd), .eq(comparator_2_eq));  // open: gt, lt
  Comparator #(.width(5)) comparator_3 (.a(EX_MEM_RegisterRd), .b({5{1'b0}}), .eq(comparator_3_eq));  // open: gt, lt
  Comparator #(.width(5)) comparator_4 (.a(MEM_WB_RegisterRd), .b({5{1'b0}}), .eq(comparator_4_eq));  // open: gt, lt
  Comparator #(.width(5)) comparator_5 (
    .a(MEM_WB_RegisterRd), .b(ID_EX_RegisterRt), .eq(comparator_5_eq));  // open: gt, lt
  and and_3 (B[1], comparator_1_eq, ~comparator_3_eq, and_1_out);  // AND_Gate
  Comparator #(.width(5)) comparator_6 (
    .a(ID_EX_RegisterRs), .b(MEM_WB_RegisterRd), .eq(comparator_6_eq));  // open: gt, lt
  and and_4 (A[1], comparator_2_eq, ~comparator_3_eq, and_1_out);  // AND_Gate
  and and_5 (B[0], comparator_5_eq, ~B[1], ~comparator_4_eq, and_2_out);  // AND_Gate
  and and_6 (A[0], comparator_6_eq, ~A[1], ~comparator_4_eq, and_2_out);  // AND_Gate
endmodule

module IF_ID (
  input  [31:0] PC_4,
  input  [24:0] TAG,
  input  [1:0] P,
  input  [31:0] INST,
  input  [31:0] Target,
  input  Branch_Guess,
  input  Flush,
  input  Disable,
  input  Clock,
  output [31:0] PC_4_2,
  output [24:0] TAG_2,
  output [1:0] P_2,
  output [31:0] INST_2,
  output [31:0] Target_2,
  output Branch_Guess_2
);

  wire not_1_out;
  wire [31:0] multiplexer_1_out;

  Multiplexer #(.width(32), .enable("false")) multiplexer_1 (
    .in0(INST), .in1({32{1'b0}}), .out(multiplexer_1_out), .sel(Flush));
  not not_1 (not_1_out, Disable);
  Register #(.width(32)) register_1 (.D(PC_4), .en(not_1_out), .Q(PC_4_2), .clk(Clock));  // open: clr
  Register #(.width(32)) register_2 (.D(multiplexer_1_out), .en(not_1_out), .Q(INST_2), .clk(Clock));  // open: clr
  Register #(.width(25)) register_3 (.D(TAG), .en(not_1_out), .Q(TAG_2), .clk(Clock));  // open: clr
  Register #(.width(2)) register_4 (.D(P), .Q(P_2), .clk(Clock));  // open: en, clr
  Register #(.width(32)) register_5 (.D(Target), .Q(Target_2), .clk(Clock));  // open: en, clr
  Register #(.width(1)) register_6 (.D(Branch_Guess), .en(not_1_out), .Q(Branch_Guess_2), .clk(Clock));  // open: clr
endmodule

module ID_EX (
  input  [31:0] PC_4,
  input  [24:0] TAG,
  input  [1:0] P,
  input  [31:0] A,
  input  [31:0] Target,
  input  [31:0] B,
  input  Branch_Guess,
  input  [31:0] imm,
  input  [4:0] shamt,
  input  [5:0] funct,
  input  [11:0] OP,
  input  Flush,
  input  [4:0] rs,
  input  [4:0] rt,
  input  [4:0] rd,
  input  Disable,
  input  Clock,
  output [31:0] PC_4_2,
  output [24:0] TAG_2,
  output [1:0] P_2,
  output [31:0] A_2,
  output [31:0] Target_2,
  output [31:0] B_2,
  output Branch_Guess_2,
  output [31:0] imm_2,
  output [4:0] shamt_2,
  output [5:0] funct_2,
  output [11:0] OP_2,
  output [4:0] rs_2,
  output [4:0] rt_2,
  output [4:0] rd_2
);

  wire not_1_out;
  wire [11:0] multiplexer_1_out;

  Multiplexer #(.width(12), .enable("false")) multiplexer_1 (
    .in0(OP), .in1({12{1'b0}}), .out(multiplexer_1_out), .sel(Flush));
  not not_1 (not_1_out, Disable);
  Register #(.width(32)) register_1 (.D(PC_4), .en(not_1_out), .Q(PC_4_2), .clk(Clock));  // open: clr
  Register #(.width(32)) register_2 (.D(A), .en(not_1_out), .Q(A_2), .clk(Clock));  // open: clr
  Register #(.width(32)) register_3 (.D(B), .en(not_1_out), .Q(B_2), .clk(Clock));  // open: clr
  Register #(.width(32)) register_4 (.D(imm), .en(not_1_out), .Q(imm_2), .clk(Clock));  // open: clr
  Register #(.width(5)) register_5 (.D(shamt), .en(not_1_out), .Q(shamt_2), .clk(Clock));  // open: clr
  Register #(.width(6)) register_6 (.D(funct), .en(not_1_out), .Q(funct_2), .clk(Clock));  // open: clr
  Register #(.width(12)) register_7 (.D(multiplexer_1_out), .en(not_1_out), .Q(OP_2), .clk(Clock));  // open: clr
  Register #(.width(5)) register_8 (.D(rs), .en(not_1_out), .Q(rs_2), .clk(Clock));  // open: clr
  Register #(.width(5)) register_9 (.D(rt), .en(not_1_out), .Q(rt_2), .clk(Clock));  // open: clr
  Register #(.width(5)) register_10 (.D(rd), .en(not_1_out), .Q(rd_2), .clk(Clock));  // open: clr
  Register #(.width(25)) register_11 (.D(TAG), .en(not_1_out), .Q(TAG_2), .clk(Clock));  // open: clr
  Register #(.width(2)) register_12 (.D(P), .en(not_1_out), .Q(P_2), .clk(Clock));  // open: clr
  Register #(.width(32)) register_13 (.D(Target), .en(not_1_out), .Q(Target_2), .clk(Clock));  // open: clr
  Register #(.width(1)) register_14 (.D(Branch_Guess), .en(not_1_out), .Q(Branch_Guess_2), .clk(Clock));  // open: clr
endmodule

module EX_MEM (
  input  [31:0] PC_4,
  input  [31:0] ALUresult,
  input  [31:0] B,
  input  [11:0] OP,
  input  [4:0] RDst,
  input  Disable,
  input  Clock,
  output [31:0] PC_4_2,
  output [31:0] ALUresult_2,
  output [31:0] B_2,
  output [11:0] OP_2,
  output [4:0] RDst_2
);

  wire not_1_out;

  not not_1 (not_1_out, Disable);
  Register #(.width(32)) register_1 (.D(PC_4), .en(not_1_out), .Q(PC_4_2), .clk(Clock));  // open: clr
  Register #(.width(32)) register_2 (.D(ALUresult), .en(not_1_out), .Q(ALUresult_2), .clk(Clock));  // open: clr
  Register #(.width(32)) register_3 (.D(B), .en(not_1_out), .Q(B_2), .clk(Clock));  // open: clr
  Register #(.width(12)) register_4 (.D(OP), .en(not_1_out), .Q(OP_2), .clk(Clock));  // open: clr
  Register #(.width(5)) register_5 (.D(RDst), .en(not_1_out), .Q(RDst_2), .clk(Clock));  // open: clr
endmodule

module MEM_WB (
  input  [31:0] PC_4,
  input  [31:0] ALUresult,
  input  [31:0] Data,
  input  [11:0] OP,
  input  [4:0] RDst,
  input  Disable,
  input  Clock,
  output [31:0] PC_4_2,
  output [31:0] ALUresult_2,
  output [31:0] Data_2,
  output [11:0] OP_2,
  output [4:0] RDst_2
);

  wire not_1_out;

  not not_1 (not_1_out, Disable);
  Register #(.width(32)) register_1 (.D(PC_4), .en(not_1_out), .Q(PC_4_2), .clk(Clock));  // open: clr
  Register #(.width(32)) register_2 (.D(ALUresult), .en(not_1_out), .Q(ALUresult_2), .clk(Clock));  // open: clr
  Register #(.width(32)) register_3 (.D(Data), .en(not_1_out), .Q(Data_2), .clk(Clock));  // open: clr
  Register #(.width(12)) register_4 (.D(OP), .en(not_1_out), .Q(OP_2), .clk(Clock));  // open: clr
  Register #(.width(5)) register_5 (.D(RDst), .en(not_1_out), .Q(RDst_2), .clk(Clock));  // open: clr
endmodule

module SUPERMUX (
  input  [4:0] in_1,
  input  in_2,
  output [4:0] out_3
);

  Multiplexer #(.width(5), .enable("false")) multiplexer_1 (.in0(in_1), .in1({5{1'b1}}), .out(out_3), .sel(in_2));
endmodule

module Branch_Guessing_Unit (
  input  [24:0] Tag,
  input  [31:0] PC,
  input  [1:0] P,
  output Out
);

  wire comparator_1_eq, comparator_2_eq, comparator_3_eq, or_1_out;

  Comparator #(.width(2)) comparator_1 (.a(P), .b(2'b10), .eq(comparator_1_eq));  // open: gt, lt
  or or_1 (or_1_out, comparator_1_eq, comparator_2_eq);
  Comparator #(.width(2)) comparator_2 (.a(P), .b(2'b11), .eq(comparator_2_eq));  // open: gt, lt
  Comparator #(.width(25)) comparator_3 (.a(Tag), .b(PC[31:7]), .eq(comparator_3_eq));  // open: gt, lt
  and and_1 (Out, comparator_3_eq, or_1_out);

  // Notes on the sheet:
  //   WT
  //   ST
endmodule

module P_unit (
  input  [1:0] P,
  input  Increment,
  output [1:0] out_3
);

  // PLA p: pin names not known; wires that end beside it: out_3

  // Notes on the sheet:
  //   Gør PLAen mindre
endmodule

module Jump_n_Branch (
  input  [31:0] PC_4,
  input  [31:0] Amux,
  input  [31:0] ImmideateExt,
  input  [5:0] ALUcontrol,
  input  ALUzero,
  input  Branch,
  input  [31:0] Target,
  input  Branch_Guess,
  output [31:0] PCnew,
  output [31:0] Target_2,
  output P_Increment,
  output Flushing
);

  wire [1:1] comparator_1_eq;
  wire [31:0] multiplexer_1_out;

  Multiplexer #(.width(32), .enable("false")) multiplexer_1 (
    .in0(PC_4), .in1(Amux), .out(multiplexer_1_out), .sel(ALUcontrol[5]));
  // Adder adder_1: pin names not known; wires that end beside it: ALUcontrol[5], ALUcontrol[5], ALUcontrol[5], ALUcontrol[5], ALUcontrol[5], ALUcontrol[5], ALUcontrol[5], multiplexer_1_out, ALUcontrol[5], ALUcontrol[5], ALUcontrol[5], ALUcontrol[5], Target_2, ALUcontrol[5], ALUcontrol[5], P_Increment, P_Increment, P_Increment, P_Increment, P_Increment, P_Increment
  and and_1 (P_Increment, ALUzero, Branch);
  Multiplexer #(.width(32), .enable("false")) multiplexer_2 (
    .in0(multiplexer_1_out), .in1(Target_2), .out(PCnew), .sel(P_Increment));
  Comparator #(.width(32)) comparator_1 (.a(PCnew), .b(Target), .eq(comparator_1_eq[1]));  // open: gt, lt
  // PLA pla_1: pin names not known; wires that end beside it: Branch_Guess, Branch_Guess, Branch_Guess, Branch_Guess, Branch_Guess, Branch_Guess, Branch_Guess, Branch_Guess, Branch_Guess, P_Increment, Branch_Guess, Branch_Guess, P_Increment, P_Increment, P_Increment, P_Increment, P_Increment, Flushing

  // Notes on the sheet:
  //   JumpR
  //   Jr
  //   Branching
  //   BEQ
endmodule
