// Logisim project g1-3.circ as structural Verilog: 4 circuits, main circuit main
module main (
  input  [1:0] op,
  input  [31:0] in,
  input  [4:0] shamt,
  output [31:0] Result
);

  ShiftUnit shiftunit_1 (.in(in), .shamt(shamt), .op(op), .result(Result));
endmodule

module ShiftUnit (
  input  [1:0] op,
  input  [31:0] in,
  input  [4:0] shamt,
  output [31:0] result
);
endmodule

module shift_left (
  input  [31:0] in,
  input  fill,
  input  [4:0] shamt,
  output [31:0] result
);

  wire [0:0] bit_extender_1_out;
  wire [1:0] bit_extender_2_out;
  wire [3:0] bit_extender_3_out;
  wire [7:0] bit_extender_4_out;
  wire [15:0] bit_extender_5_out;
  wire [31:0] multiplexer_1_out, multiplexer_2_out, multiplexer_3_out, multiplexer_4_out;

  Bit_Extender #(.in_width(1), .out_width(1), .\type ("sign")) bit_extender_1 (.in(fill), .out(bit_extender_1_out[0]));
  Multiplexer #(.width(32), .enable("false")) multiplexer_1 (
    .in0(in), .in1({in[30:0], bit_extender_1_out[0]}), .out(multiplexer_1_out), .sel(shamt[0]));
  assign bit_extender_2_out = {{1{fill}}, fill};  // Bit_Extender bit_extender_2
  Multiplexer #(.width(32), .enable("false")) multiplexer_2 (
    .in0(multiplexer_1_out), .in1({multiplexer_1_out[29:0], bit_extender_2_out}), .out(multiplexer_2_out),
    .sel(shamt[1]));
  assign bit_extender_3_out = {{3{fill}}, fill};  // Bit_Extender bit_extender_3
  Multiplexer #(.width(32), .enable("false")) multiplexer_3 (
    .in0(multiplexer_2_out), .in1({multiplexer_2_out[27:0], bit_extender_3_out}), .out(multiplexer_3_out),
    .sel(shamt[2]));
  assign bit_extender_4_out = {{7{fill}}, fill};  // Bit_Extender bit_extender_4
  Multiplexer #(.width(32), .enable("false")) multiplexer_4 (
    .in0(multiplexer_3_out), .in1({multiplexer_3_out[23:0], bit_extender_4_out}), .out(multiplexer_4_out),
    .sel(shamt[3]));
  assign bit_extender_5_out = {{15{fill}}, fill};  // Bit_Extender bit_extender_5
  Multiplexer #(.width(32), .enable("false")) multiplexer_5 (
    .in0(multiplexer_4_out), .in1({multiplexer_4_out[15:0], bit_extender_5_out}), .out(result), .sel(shamt[4]));
endmodule

module shift_right (
  input  [31:0] in,
  input  fill,
  input  [4:0] shamt,
  output [31:0] result
);

  wire [1:0] bit_extender_2_out;
  wire [3:0] bit_extender_3_out;
  wire [7:0] bit_extender_4_out;
  wire [15:0] bit_extender_5_out;
  wire [31:0] multiplexer_1_out, multiplexer_2_out, multiplexer_3_out, multiplexer_4_out;
  wire [31:31] bit_extender_1_out;

  Bit_Extender #(.in_width(1), .out_width(1), .\type ("sign")) bit_extender_1 (.in(fill), .out(bit_extender_1_out[31]));
  Multiplexer #(.width(32), .enable("false")) multiplexer_1 (
    .in0(in), .in1({bit_extender_1_out[31], in[31:1]}), .out(multiplexer_1_out), .sel(shamt[0]));
  assign bit_extender_2_out = {{1{fill}}, fill};  // Bit_Extender bit_extender_2
  Multiplexer #(.width(32), .enable("false")) multiplexer_2 (
    .in0(multiplexer_1_out), .in1({multiplexer_1_out[29:0], bit_extender_2_out}), .out(multiplexer_2_out),
    .sel(shamt[1]));
  assign bit_extender_3_out = {{3{fill}}, fill};  // Bit_Extender bit_extender_3
  Multiplexer #(.width(32), .enable("false")) multiplexer_3 (
    .in0(multiplexer_2_out), .in1({multiplexer_2_out[27:0], bit_extender_3_out}), .out(multiplexer_3_out),
    .sel(shamt[2]));
  assign bit_extender_4_out = {{7{fill}}, fill};  // Bit_Extender bit_extender_4
  Multiplexer #(.width(32), .enable("false")) multiplexer_4 (
    .in0(multiplexer_3_out), .in1({multiplexer_3_out[23:0], bit_extender_4_out}), .out(multiplexer_4_out),
    .sel(shamt[3]));
  assign bit_extender_5_out = {{15{fill}}, fill};  // Bit_Extender bit_extender_5
  Multiplexer #(.width(32), .enable("false")) multiplexer_5 (
    .in0(multiplexer_4_out), .in1({multiplexer_4_out[15:0], bit_extender_5_out}), .out(result), .sel(shamt[4]));
endmodule
